// Logisim project BCD-adder.circ as structural Verilog: 4 circuits, main circuit BCD-adder
module BCD_adder (
  input  [3:0] A,
  input  [3:0] B,
  input  CI,
  output [3:0] S,
  output CO,
  output CO_2
);

  wire and_1_out, and_2_out, n4bits_adder_1_co, or_2_out;
  wire [3:0] n4bits_adder_1_s0;

  or or_1 (CO, n4bits_adder_1_co, or_2_out);
  or or_2 (or_2_out, and_1_out, and_2_out);
  _4bits_adder u_4bits_adder_1 (
    .A(A), .B(B), .CI(CI), .CO(n4bits_adder_1_co), .S3(n4bits_adder_1_s0[3]), .S2(n4bits_adder_1_s0[2]),
    .S1(n4bits_adder_1_s0[1]), .S0(n4bits_adder_1_s0[0]));
  and and_1 (and_1_out, n4bits_adder_1_s0[3], n4bits_adder_1_s0[2]);
  and and_2 (and_2_out, n4bits_adder_1_s0[1], n4bits_adder_1_s0[0]);
  _4bits_adder u_4bits_adder_2 (
    .A({1'b0, {2{CO}}, 1'b0}), .B(n4bits_adder_1_s0), .CI(1'b0), .CO(CO_2), .S3(S[3]), .S2(S[2]), .S1(S[1]),
    .S0(S[0]));
endmodule

module _4bits_adder (
  input  [3:0] A,
  input  [3:0] B,
  input  CI,
  output CO,
  output S3,
  output S2,
  output S1,
  output S0
);

  wire full_adder_1_co, full_adder_2_co, full_adder_3_co;

  full_adder full_adder_1 (.S0(S0), .CO(full_adder_1_co), .A0(B[0]), .B0(CI), .CI(A[0]));
  full_adder full_adder_2 (.S0(S1), .CO(full_adder_2_co), .A0(B[1]), .B0(full_adder_1_co), .CI(A[1]));
  full_adder full_adder_3 (.S0(S2), .CO(full_adder_3_co), .A0(B[2]), .B0(full_adder_2_co), .CI(A[2]));
  full_adder full_adder_4 (.S0(S3), .CO(CO), .A0(B[3]), .B0(full_adder_3_co), .CI(A[3]));
endmodule

module half_adder (
  input  A,
  input  B,
  output S,
  output CO
);

  xor xor_1 (S, A, B);
  and and_1 (CO, A, B);
endmodule

module full_adder (
  input  A0,
  input  B0,
  input  CI,
  output S0,
  output CO
);

  wire half_adder_1_co, half_adder_1_s, half_adder_2_co;

  half_adder half_adder_1 (.S(half_adder_1_s), .CO(half_adder_1_co), .A(A0), .B(B0));
  half_adder half_adder_2 (.S(S0), .CO(half_adder_2_co), .A(CI), .B(half_adder_1_s));
  or or_1 (CO, half_adder_2_co, half_adder_1_co);
endmodule
