// Logisim project adder.circ as structural Verilog: 6 circuits, main circuit main
module main (
  input  in_1
);
endmodule

module halfadder (
  input  A,
  input  B,
  output S,
  output CO
);

  xor xor_1 (S, A, B);
  and and_1 (CO, A, B);
endmodule

module fulladder (
  input  A0,
  input  B0,
  input  CI,
  output S0,
  output CO
);

  wire and_1_out, and_2_out, and_3_out, or_1_out, or_2_out, xor_1_out;

  and and_1 (and_1_out, A0, B0);
  and and_2 (and_2_out, A0, CI);
  and and_3 (and_3_out, B0, CI);
  xor xor_1 (xor_1_out, A0, B0);
  xor xor_2 (S0, xor_1_out, CI);
  or or_1 (or_1_out, and_1_out, and_2_out);
  or or_2 (or_2_out, and_2_out, and_3_out);
  or or_3 (CO, or_1_out, or_2_out);
endmodule

module fulladder2 (
  input  A0,
  input  B0,
  input  CI,
  output S0,
  output CO
);

  wire halfadder_1_co, halfadder_2_co, halfadder_2_s;

  halfadder halfadder_1 (.S(S0), .CO(halfadder_1_co), .A(CI), .B(halfadder_2_s));
  halfadder halfadder_2 (.S(halfadder_2_s), .CO(halfadder_2_co), .A(A0), .B(B0));
  or or_1 (CO, halfadder_1_co, halfadder_2_co);
endmodule

module _4bits_adder (
  input  [3:0] A,
  input  [3:0] B,
  input  CI,
  output CO,
  output S3,
  output S2,
  output S1,
  output S0
);

  wire fulladder2_1_co, fulladder2_2_co, fulladder2_3_co;

  fulladder2 fulladder2_1 (.S0(S0), .CO(fulladder2_1_co), .A0(A[0]), .B0(B[0]), .CI(CI));
  fulladder2 fulladder2_2 (.S0(S1), .CO(fulladder2_2_co), .A0(A[1]), .B0(B[1]), .CI(fulladder2_1_co));
  fulladder2 fulladder2_3 (.S0(S2), .CO(fulladder2_3_co), .A0(A[2]), .B0(B[2]), .CI(fulladder2_2_co));
  fulladder2 fulladder2_4 (.S0(S3), .CO(CO), .A0(A[3]), .B0(B[3]), .CI(fulladder2_3_co));
endmodule

module _8bits_adder (
  input  [3:0] A1,
  input  [3:0] A0,
  input  Ci,
  input  [3:0] B1,
  input  [3:0] B0,
  output CO,
  output [3:0] S1,
  output [3:0] S0
);

  wire n4bits_adder_1_co;

  _4bits_adder u_4bits_adder_1 (
    .A(A0), .B(B0), .CI(Ci), .CO(n4bits_adder_1_co), .S3(S0[3]), .S2(S0[2]), .S1(S0[1]), .S0(S0[0]));
  _4bits_adder u_4bits_adder_2 (
    .A(A1), .B(B1), .CI(n4bits_adder_1_co), .CO(CO), .S3(S1[3]), .S2(S1[2]), .S1(S1[1]), .S0(S1[0]));

  // Notes on the sheet:
  //   +
  //   =
endmodule
