// Logisim project class01.1.circ as structural Verilog: 1 circuit, main circuit main
module main (
  input  a,
  input  b,
  input  c,
  input  d,
  output x
);

  wire AND01_out, not_1_out, NOT_a_out, OR01_out;

  not NOT_a (NOT_a_out, a);
  and AND01 (AND01_out, NOT_a_out, b, c);
  or OR01 (OR01_out, a, d);
  not not_1 (not_1_out, OR01_out);
  and AND02 (x, AND01_out, not_1_out);

  // Notes on the sheet:
  //   class01.1: ~abc~(a+d)
endmodule
