// Logisim project class01.circ as structural Verilog: 1 circuit, main circuit main
module main (
  input  x,
  input  x1,
  input  y1,
  input  y,
  output f1,
  output f
);

  wire AND01_out, AND02_out, NOT_x_out, NOT_y_out;

  not NOT_x (NOT_x_out, x);
  not NOT_y (NOT_y_out, y);
  and AND01 (AND01_out, NOT_x_out, y);
  and AND02 (AND02_out, x, NOT_y_out);
  or OR01 (f, AND01_out, AND02_out);
  xor XOR (f1, x1, y1);

  // Notes on the sheet:
  //   class01: ~xy + x~y
  //   class01: ~xy + x~y
  //   using XOR gate
endmodule
