// Logisim project class02.2.circ as structural Verilog: 1 circuit, main circuit main
module main (
  input  A,
  input  B,
  input  C,
  input  D,
  output S
);

  wire AND01_out, AND02_out, AND03_out, AND04_out, NOT_A_out, NOT_B_out, NOT_C_out, NOT_D_out;

  not NOT_A (NOT_A_out, A);
  not NOT_C (NOT_C_out, C);
  not NOT_D (NOT_D_out, D);
  not NOT_B (NOT_B_out, B);
  and AND01 (AND01_out, NOT_A_out, B, NOT_C_out, NOT_D_out);
  and AND02 (AND02_out, NOT_A_out, B, C, NOT_D_out);
  and AND03 (AND03_out, A, NOT_B_out, NOT_C_out, NOT_D_out);
  and AND04 (AND04_out, A, NOT_B_out, C, D);
  or OR01 (S, AND01_out, AND02_out, AND03_out, AND04_out);

  // Notes on the sheet:
  //   class02.2: ~AB~C~D+~ABC~D+A~B~C~D+A~BCD
endmodule
