// Logisim project class02.4.circ as structural Verilog: 1 circuit, main circuit main
module main (
  input  A,
  input  B,
  input  A_2,
  input  B_2,
  output S,
  output S_2
);

  wire NOT_A_out, NOT_B_out, OR01_out, OR02_out;

  not NOT_B (NOT_B_out, B);
  not NOT_A (NOT_A_out, A);
  or OR01 (OR01_out, A, B);
  or OR02 (OR02_out, NOT_A_out, NOT_B_out);
  and AND01 (S_2, OR01_out, OR02_out);
  xor XOR01 (S, A_2, B_2);

  // Notes on the sheet:
  //   class02.4: (A+B)(~A+~B)
  //   using a XOR
endmodule
