// Logisim project class02.circ as structural Verilog: 1 circuit, main circuit main
module main (
  input  A,
  input  X,
  input  B,
  input  Y,
  output Z,
  output S
);

  wire AND01_out, AND02_out, not_1_out, NOT_A_out;

  not NOT_A (NOT_A_out, A);
  not not_1 (not_1_out, B);
  and AND01 (AND01_out, NOT_A_out, B);
  and AND02 (AND02_out, A, not_1_out);
  or OR01 (S, AND01_out, AND02_out);
  xor XOR01 (Z, X, Y);

  // Notes on the sheet:
  //   class02: ~AB+A~B
  //   using a XOR gate
endmodule
