// Logisim project class03.circ as structural Verilog: 1 circuit, main circuit main
module main (
  input  A,
  input  B,
  input  A_2,
  input  C,
  input  B_2,
  input  C_2,
  output Z,
  output S
);

  wire AND01_out, AND02_out, AND03_out, AND04_out, AND05_out, AND06_out, AND07_out, AND08_out, and_1_out,
       and_2_out, and_3_out, and_4_out, and_5_out, not_1_out, not_2_out, not_3_out, NOT_A_out, NOT_B_out,
       NOT_C_out, OR01_out, OR02_out, OR03_out;

  not NOT_A (NOT_A_out, A_2);
  not NOT_B (NOT_B_out, B_2);
  and AND01 (AND01_out, NOT_A_out, NOT_B_out);
  not NOT_C (NOT_C_out, C_2);
  and AND06 (AND06_out, A_2, B_2);
  and AND03 (AND03_out, AND01_out, C_2);
  and AND02 (AND02_out, AND01_out, NOT_C_out);
  and AND04 (AND04_out, NOT_B_out, NOT_C_out);
  and AND07 (AND07_out, AND06_out, NOT_C_out);
  and AND08 (AND08_out, AND06_out, C_2);
  or OR01 (OR01_out, AND03_out, AND02_out);
  and AND05 (AND05_out, A_2, AND04_out);
  or OR02 (OR02_out, OR01_out, AND05_out);
  or OR03 (OR03_out, OR02_out, AND07_out);
  or OR04 (S, OR03_out, AND08_out);
  not not_1 (not_1_out, A);
  not not_2 (not_2_out, B);
  not not_3 (not_3_out, C);
  and and_1 (and_1_out, A, B, C);
  and and_2 (and_2_out, A, B, not_3_out);
  and and_3 (and_3_out, not_1_out, not_2_out, C);
  and and_4 (and_4_out, A, not_1_out, not_2_out);
  and and_5 (and_5_out, not_1_out, not_2_out, not_3_out);
  or or_1 (Z, and_1_out, and_2_out, and_3_out, and_4_out, and_5_out);

  // Notes on the sheet:
  //   Simplification by Boolean Algebra
  //   class03: ~A~B~C+~A~BC+A~B~C+AB~C+ABC
endmodule
