// Logisim project magnitudesignal- comparator.circ as structural Verilog: 2 circuits, main circuit main
module main (
  input  A,
  input  B,
  output S
);

  xnor xnor_1 (S, A, B);
endmodule

// S
module _8bits_comparator (
  input  [7:0] A,
  input  [7:0] B,
  output S
);

  wire and_1_out, and_2_out, and_3_out, and_4_out, and_5_out, and_6_out, xnor_1_out, xnor_2_out, xnor_3_out,
       xnor_4_out, xnor_5_out, xnor_6_out, xnor_7_out, xnor_8_out;

  xnor xnor_1 (xnor_1_out, A[7], B[7]);
  xnor xnor_2 (xnor_2_out, A[6], B[6]);
  xnor xnor_3 (xnor_3_out, A[5], B[5]);
  xnor xnor_4 (xnor_4_out, A[4], B[4]);
  xnor xnor_5 (xnor_5_out, A[3], B[3]);
  xnor xnor_6 (xnor_6_out, A[2], B[2]);
  xnor xnor_7 (xnor_7_out, A[1], B[1]);
  xnor xnor_8 (xnor_8_out, A[0], B[0]);
  and and_1 (and_1_out, xnor_1_out, xnor_2_out);
  and and_2 (and_2_out, and_1_out, and_3_out);
  and and_3 (and_3_out, xnor_3_out, xnor_4_out);
  and and_4 (and_4_out, xnor_5_out, xnor_6_out);
  and and_5 (and_5_out, and_4_out, and_6_out);
  and and_6 (and_6_out, xnor_7_out, xnor_8_out);
  and and_7 (S, and_2_out, and_5_out);
endmodule
