// Logisim project multiplier.circ as structural Verilog
module _2bits_multiplier (
  input  [1:0] A,
  input  [1:0] B,
  output [3:0] C
);

  wire and_1_out, and_2_out, and_3_out, half_adder_1_co;

  and and_1 (and_1_out, A[1], B[0]);
  and and_2 (and_2_out, A[1], B[1]);
  half_adder half_adder_1 (.S(C[1]), .CO(half_adder_1_co), .A(and_3_out), .B(and_1_out));
  half_adder half_adder_2 (.S(C[2]), .CO(C[3]), .A(half_adder_1_co), .B(and_2_out));
  and and_3 (and_3_out, A[0], B[1]);
  and and_4 (C[0], B[0], A[0]);
endmodule

module half_adder (
  input  A,
  input  B,
  output S,
  output CO
);

  xor xor_1 (S, A, B);
  and and_1 (CO, A, B);
endmodule

module _2x3bits_multiplier (
  input  [3:0] B,
  input  [2:0] A
);

  half_adder half_adder_1 (.A(A[0]), .B(B[0]));  // open: S, CO
endmodule

module full_adder (
  input  A0,
  input  B0,
  input  CI,
  output S0,
  output CO
);

  wire half_adder_1_co, half_adder_1_s, half_adder_2_co;

  half_adder half_adder_1 (.S(half_adder_1_s), .CO(half_adder_1_co), .A(A0), .B(B0));
  half_adder half_adder_2 (.S(S0), .CO(half_adder_2_co), .A(CI), .B(half_adder_1_s));
  or or_1 (CO, half_adder_2_co, half_adder_1_co);
endmodule
