// Logisim project project.circ as structural Verilog: 1 circuit, main circuit main
module main (
  input  I,
  input  U,
  input  T,
  output F
);

  wire and_1_out, not_1_out, not_2_out;

  not not_1 (not_1_out, I);
  not not_2 (not_2_out, T);
  and and_1 (and_1_out, not_1_out, not_2_out);
  or or_1 (F, and_1_out, U);
endmodule
