// Logisim project subtractor.circ as structural Verilog
module half_subtractor (
  input  A,
  input  B,
  output S0,
  output t0
);

  xor xor_1 (S0, A, B);
  and and_1 (t0, ~A, B);  // AND_Gate
endmodule

module full_adder (
  input  A,
  input  B,
  input  CI,
  output S0,
  output CO
);

  wire and_1_out, and_2_out, and_3_out, or_1_out, or_2_out, xor_1_out;

  xor xor_1 (xor_1_out, A, B);
  xor xor_2 (S0, xor_1_out, CI);
  and and_1 (and_1_out, A, B);
  or or_1 (or_1_out, and_1_out, and_2_out);
  and and_2 (and_2_out, A, CI);
  or or_2 (or_2_out, and_2_out, and_3_out);
  and and_3 (and_3_out, B, CI);
  or or_3 (CO, or_1_out, or_2_out);
endmodule

module full_subtractor (
  input  A,
  input  B,
  input  T0,
  output S0,
  output t0_2
);

  wire and_1_out, and_2_out, and_3_out, or_1_out, or_2_out, xor_1_out;

  xor xor_1 (xor_1_out, A, B);
  and and_1 (and_1_out, ~A, T0);  // AND_Gate
  and and_2 (and_2_out, ~A, B);  // AND_Gate
  and and_3 (and_3_out, B, T0);
  xor xor_2 (S0, xor_1_out, T0);
  or or_1 (or_1_out, and_1_out, and_2_out);
  or or_2 (or_2_out, and_2_out, and_3_out);
  or or_3 (t0_2, or_1_out, or_2_out);
endmodule

module _4bits_adder_subtractor (
  input  m,
  input  A0,
  input  B0,
  input  A1,
  input  B1,
  input  A2,
  input  B2,
  input  A3,
  input  B3,
  output CO,
  output S3,
  output S2,
  output S1,
  output S0
);

  wire full_adder2_1_co, full_adder2_2_co, full_adder2_3_co, xor_1_out, xor_2_out, xor_3_out, xor_4_out;

  full_adder2 full_adder2_1 (.S0(S0), .CO(full_adder2_1_co), .A0(xor_1_out), .B0(A0), .CI(m));
  xor xor_1 (xor_1_out, B0, m);
  full_adder2 full_adder2_2 (.S0(S1), .CO(full_adder2_2_co), .A0(xor_2_out), .B0(A1), .CI(full_adder2_1_co));
  xor xor_2 (xor_2_out, B1, m);
  full_adder2 full_adder2_3 (.S0(S2), .CO(full_adder2_3_co), .A0(xor_3_out), .B0(A2), .CI(full_adder2_2_co));
  xor xor_3 (xor_3_out, B2, m);
  full_adder2 full_adder2_4 (.S0(S3), .CO(CO), .A0(xor_4_out), .B0(A3), .CI(full_adder2_3_co));
  xor xor_4 (xor_4_out, B3, m);

  // Notes on the sheet:
  //   0 == sum / 1 == sub
  //   XOR = C1
  //   no overflow in sub*
  //   bit1 + C2(bit)
endmodule

module _4bits_fulladder (
  input  [3:0] A,
  input  [3:0] B,
  input  CI,
  output CO,
  output S3,
  output S2,
  output S1,
  output S0
);

  wire full_adder_1_co, full_adder_2_co, full_adder_3_co;

  full_adder full_adder_1 (.A(B[0]), .B(CI), .CI(A[0]), .S0(S0), .CO(full_adder_1_co));
  full_adder full_adder_2 (.A(B[1]), .B(full_adder_1_co), .CI(A[1]), .S0(S1), .CO(full_adder_2_co));
  full_adder full_adder_3 (.A(B[2]), .B(full_adder_2_co), .CI(A[2]), .S0(S2), .CO(full_adder_3_co));
  full_adder full_adder_4 (.A(B[3]), .B(full_adder_3_co), .CI(A[3]), .S0(S3), .CO(CO));
endmodule

module full_adder2 (
  input  A0,
  input  B0,
  input  CI,
  output S0,
  output CO
);

  wire half_adder2_1_co, half_adder2_1_s, half_adder2_2_co;

  half_adder2 half_adder2_1 (.S(half_adder2_1_s), .CO(half_adder2_1_co), .A(A0), .B(B0));
  half_adder2 half_adder2_2 (.S(S0), .CO(half_adder2_2_co), .A(CI), .B(half_adder2_1_s));
  or or_1 (CO, half_adder2_2_co, half_adder2_1_co);
endmodule

module half_adder2 (
  input  A,
  input  B,
  output S,
  output CO
);

  xor xor_1 (S, A, B);
  and and_1 (CO, A, B);
endmodule
