// Logisim project truthtable.circ as structural Verilog: 2 circuits, main circuit minterms
module minterms (
  input  A,
  input  B,
  input  C,
  output S
);

  wire and_1_out, and_2_out, and_3_out, and_4_out, and_5_out, and_6_out, not_1_out, not_2_out, not_3_out,
       or_1_out;

  not not_1 (not_1_out, A);
  not not_2 (not_2_out, B);
  not not_3 (not_3_out, C);
  and and_1 (and_1_out, not_1_out, B);
  and and_2 (and_2_out, A, not_2_out);
  and and_3 (and_3_out, A, not_2_out);
  and and_4 (and_4_out, and_1_out, not_3_out);
  and and_5 (and_5_out, and_2_out, not_3_out);
  and and_6 (and_6_out, and_3_out, C);
  or or_1 (or_1_out, and_4_out, and_5_out);
  or or_2 (S, or_1_out, and_6_out);

  // Notes on the sheet:
  //   S = (A'BC')+(AB'C')+(AB'C)
  //   minterms
endmodule

module maxterms (
  input  A,
  input  B,
  input  C,
  output S
);

  wire and_1_out, not_1_out, not_2_out, not_3_out, or_1_out, or_2_out, or_3_out, or_4_out, or_5_out, or_6_out;

  not not_1 (not_1_out, A);
  not not_2 (not_2_out, B);
  not not_3 (not_3_out, C);
  or or_1 (or_1_out, A, B);
  or or_2 (or_2_out, not_1_out, B);
  or or_3 (or_3_out, not_1_out, not_2_out);
  or or_4 (or_4_out, or_1_out, not_3_out);
  or or_5 (or_5_out, or_2_out, not_3_out);
  or or_6 (or_6_out, or_3_out, C);
  and and_1 (and_1_out, or_4_out, or_5_out);
  and and_2 (S, and_1_out, or_6_out);

  // Notes on the sheet:
  //   S = (A+B+C')(A'+B+C')(A'+B'+C)
  //   Maxterms
endmodule
