// Logisim project universal_gate(NAND).circ as structural Verilog: 3 circuits, main circuit NOT
module NOT (
  input  A,
  output s0
);

  nand nand_1 (s0, A, A);
  // NOT_Gate not_1 is placed but not wired

  // Notes on the sheet:
  //   NOT
  //   NAND(A,A) = NOT(A)
  //   S0 = ~(AA) 
  //   S0 = ~A
  //   A
  //   ~A
  //   A
  //   ~A
endmodule

module AND (
  input  A,
  input  B,
  output s0
);

  wire nand_1_out;

  nand nand_1 (nand_1_out, A, B);
  // AND_Gate and_1 is placed but not wired
  nand nand_2 (s0, nand_1_out, nand_1_out);

  // Notes on the sheet:
  //   S0 = ~(~(AB))
  //   S0 = AB
  //   AND
  //   NAND(NAND(A,B)) = AND(A,B)
  //   S0 = ~(~(AB)~(AB))
  //   A
  //   ~(AB)
  //   B
  //   ~(AB)
  //   AB
  //   ~(AB)
  //   Dupla negação*
  //   AB
endmodule

module OR (
  input  A,
  input  B,
  output s0
);

  wire nand_1_out, nand_2_out;

  nand nand_1 (nand_1_out, A, A);
  nand nand_2 (nand_2_out, B, B);
  // OR_Gate or_1 is placed but not wired
  nand nand_3 (s0, nand_1_out, nand_2_out);

  // Notes on the sheet:
  //   S0 = ~(~A~B)
  //   S0 = A+B
  //   OR
  //   NAND(NAND(A,A),NAND(B,B)) = OR(A,B)
  //   S0 = ~(~(AA)~(BB))
  //   A
  //   ~A
  //   A
  //   B
  //   ~B
  //   B
  //   De Morgan*
  //   ~(~A~B)
  //   A+B
  //   A+B
endmodule
