// Logisim project universal_gate(NOR).circ as structural Verilog: 3 circuits, main circuit NOT
module NOT (
  input  A,
  output s0
);

  nor nor_1 (s0, A, A);
  // NOT_Gate not_1 is placed but not wired

  // Notes on the sheet:
  //   NOT
  //   NOR(A,A) = NOT(A)
  //   S0 = ~(A+A) 
  //   S0 = ~A
  //   A
  //   ~A
  //   A
  //   ~A
endmodule

module AND (
  input  A,
  input  B,
  output s0
);

  wire nor_1_out, nor_2_out;

  nor nor_1 (nor_1_out, A, A);
  nor nor_2 (nor_2_out, B, B);
  // AND_Gate and_1 is placed but not wired
  nor nor_3 (s0, nor_1_out, nor_2_out);

  // Notes on the sheet:
  //   S0 = ~(~A+~B)
  //   S0 = AB
  //   AND
  //   NOR(NOR(A,A),NOR(B,B)) = OR(A,B)
  //   S0 = ~(~(A+A)+~(B+B))
  //   A
  //   ~A
  //   A
  //   B
  //   ~B
  //   B
  //   De Morgan*
  //   ~A
  //   ~(~A+~B)
  //   ~B
  //   AB
endmodule

module OR (
  input  A,
  input  B,
  output s0
);

  wire nor_1_out;

  // OR_Gate or_1 is placed but not wired
  nor nor_1 (nor_1_out, A, B);
  nor nor_2 (s0, nor_1_out, nor_1_out);

  // Notes on the sheet:
  //   OR
  //   NOR(NOR(A,B)) = AND(A,B)
  //   S0 = ~(~(A+B)+~(A+B))
  //   S0 = ~(~(A+B))
  //   S0 = A+B
  //   A
  //   ~(A+B)
  //   B
  //   ~(A+B)
  //   ~(A+B)
  //   Dupla negação*
  //   ~(~(A+B))
  //   A+B
endmodule
